# Fritzing sketch Transmitter (saved by Fritzing 0.9.3b)

parts:
  hc-sr1 = hc-sr04
  hc-sr2 = hc-sr04
  Part1 = Arduino Mega ADK (Rev3)
  U1 = GAS_SENSOR [package=mq-3]

nets:
  VCC: hc-sr1.VCC, hc-sr2.VCC, Part1.5V
  GND: hc-sr1.GND, hc-sr2.GND, Part1.GND, U1.H2
  N1: Part1.A0, U1.A1
  N2: Part1.3V3, U1.B1
